// Digital circuit 74195.dig as structural Verilog
module _74195 (
  input  CLRn,
  input  CLK,
  input  SH_LDn,
  input  A,
  input  B,
  input  C,
  input  D,
  input  J,
  input  Kn,
  input  VCC,
  input  GND,
  output QD,
  output QC,
  output QB,
  output QA,
  output QDn
);

  wire and_1_out, multiplexer_1_out, multiplexer_2_out, multiplexer_3_out, multiplexer_4_out,
       multiplexer_5_out, multiplexer_6_out, not_1_out, QA_nq;

  PowerSupply powersupply_1 (.VDD(VCC), .GND(GND));
  not not_1 (not_1_out, CLRn);
  and and_1 (and_1_out, ~J, Kn);  // And
  Multiplexer #(.Selector_Bits(2)) multiplexer_1 (
    .sel({J, Kn}), .in_0(1'b0), .in_1(A), .in_2(QA_nq), .in_3(1'b1), .out(multiplexer_1_out));
  Multiplexer multiplexer_2 (.sel(and_1_out), .in_0(QA), .in_1(A), .out(multiplexer_2_out));
  Multiplexer multiplexer_3 (.sel(SH_LDn), .in_0(A), .in_1(multiplexer_1_out), .out(multiplexer_3_out));
  D_FF_AS u_QA (.Set(1'b0), .D(multiplexer_3_out), .C(CLK), .Clr(not_1_out), .Q(QA), .nQ(QA_nq));
  Multiplexer multiplexer_4 (.sel(SH_LDn), .in_0(B), .in_1(multiplexer_2_out), .out(multiplexer_4_out));
  D_FF_AS u_QB (.Set(1'b0), .D(multiplexer_4_out), .C(CLK), .Clr(not_1_out), .Q(QB));  // open: nQ
  Multiplexer multiplexer_5 (.sel(SH_LDn), .in_0(C), .in_1(QB), .out(multiplexer_5_out));
  D_FF_AS u_QC (.Set(1'b0), .D(multiplexer_5_out), .C(CLK), .Clr(not_1_out), .Q(QC));  // open: nQ
  Multiplexer multiplexer_6 (.sel(SH_LDn), .in_0(D), .in_1(QC), .out(multiplexer_6_out));
  D_FF_AS u_QD (.Set(1'b0), .D(multiplexer_6_out), .C(CLK), .Clr(not_1_out), .Q(QD), .nQ(QDn));

  // Notes on the sheet:
  //   CLRn: pin 1
  //   QD: pin 12
  //   QC: pin 13
  //   QB: pin 14
  //   QA: pin 15
  //   QDn: pin 11
  //   CLK: pin 10
  //   SH_LDn: pin 9
  //   A: pin 4
  //   B: pin 5
  //   C: pin 6
  //   D: pin 7
  //   J: pin 2
  //   Kn: pin 3
  //   VCC: pin 16, default 1
  //   GND: pin 8
endmodule
